# Fritzing sketch weather_station (saved by Fritzing 0.9.6b)
breadboards: 2

parts:
  M1 = DOIT Esp32 DevKit v1 (30 pins long, 11 pins width) [part_number=ESP32S-PIN30]
  Squix1 = OLED 0.96" 128x64 I2C SSD1306
  Onderdeel1 = Barometric Pressure Sensor - BMP180 Breakout (GY-68)
  AM1 = AM2320 Humidity and Temperature Sensor [part_number="Adafruit #3721"]
  Onderdeel2 = BH1750

nets:
  VCC: M1.3V3, Squix1.VCC, Onderdeel1.VCC, AM1.VDD, Onderdeel2.VCC
  GND: M1.GND, M1.D5, Squix1.GND, Onderdeel1.GND, AM1.GND, Onderdeel2.GND
  N1: M1.D21, Squix1.SCA, Onderdeel1.SDA, AM1.SDA, Onderdeel2.SDA
  N2: M1.D22, Squix1.SCL, Onderdeel1.SCL, AM1.SCL, Onderdeel2.SCL

notes:
  GND
  SDA
  VCC
  SCL

custom parts:
  DOIT Esp32 DevKit v1 (30 pins long, 11 pins width): The DOIT Esp32 DevKit v1 is one of the development board created by DOIT to evaluate the ESP-WROOM-32 module. It is based on the ESP32 microcontroller that boasts Wifi, Bluetooth, Ethernet and Low Power support all in a single chip. (vanepp) made breadboard work, adjusted pin numbering and labels and reduced size of schematic and cleaned up pcb. This chip is 30pins long (2 x15) and 11 pins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
  AM2320 Humidity and Temperature Sensor: AM2320 I2C Humidity and Temperature Sensor
  BH1750: Light Sensor
